# Fritzing sketch Sensors_1 (saved by Fritzing 0.9.3b)

parts:
  U1 = ESP32-38PinWide [part_number=ESP32-38PinWide]
  DHT1 = DHT11 Humitidy and Temperature Sensor
  YL-83_-_Detection_Board1 = YL-83 Rain Sensor - Detection Board
  YL-83_-_Control_Board1 = YL-83 Rain Sensor - Control Board
  IC1 = Voltage Regulator [package=to-220-alt]
  VCC1 = 4 x AAA Battery Mount
  C1 = Electrolytic Capacitor [capacitance=1µF package="100 mil [THT, electrolytic]"]
  U2 = GAS_SENSOR [package=mq-3]
  S1 = Magnetic Door Switch [package=reed_switch_plastic]
  R1 = Resistor [tolerance=±5% resistance=220 package=THT]

nets:
  N1: U1.3.3, DHT1.NULL
  N2: U1.GPIO34, S1.1, R1.Pin_0
  GND: U1.GND, DHT1.GND, YL-83_-_Control_Board1.GND, U2.A1, R1.Pin_1
  VIN: U1.VIN, YL-83_-_Control_Board1.VCC, IC1.OUT, C1.-, U2.B1, S1.2
  N3: U1.GPIO16, DHT1.DATA
  N4: U1.GPIO5, YL-83_-_Control_Board1.DO
  N5: YL-83_-_Detection_Board1.POS, YL-83_-_Control_Board1.POS
  N6: YL-83_-_Detection_Board1.NEG, YL-83_-_Control_Board1.NEG
  N7: IC1.GND, VCC1.+
  N8: IC1.IN, VCC1.-, C1.+

notes:
  Gas Sensor
  Door Switch

custom parts:
  ESP32-38PinWide: Generic 38-Pin ESP32 with wide format (only access to one side of pins on a breadboard) based on Stephen Lilley's HiLetgo ESP-WROOM-32 ESP32 ESP-32S Development Board.
  DHT11 Humitidy and Temperature Sensor: DHT11 Humidity and Temperature Sensor
  YL-83 Rain Sensor - Detection Board: The YL-83 is a rain sensor that has more resistance when dry and less resistance when wet. The module runs at 5V.
  YL-83 Rain Sensor - Control Board: The YL-83 is a rain sensor that has more resistance when dry and less resistance when wet. The module runs at 5V.
